// Logisim project AZ21_2.circ as structural Verilog: 1 circuit, main circuit main
module main (
  input  Mode,
  input  Sin
);

  wire and_1_out, and_2_out, and_3_out, and_4_out, and_5_out, and_6_out, and_7_out, and_8_out, Clock_out,
       d_ff_1_q, d_ff_2_q, d_ff_3_q, d_ff_4_q, not_1_out, or_1_out, or_2_out, or_3_out, or_4_out;

  not not_1 (not_1_out, Mode);
  and and_1 (and_1_out, Sin, Mode);
  and and_2 (and_2_out, not_1_out, d_ff_2_q);
  and and_3 (and_3_out, d_ff_1_q, Mode);
  and and_4 (and_4_out, not_1_out, d_ff_3_q);
  and and_5 (and_5_out, d_ff_2_q, Mode);
  and and_6 (and_6_out, not_1_out, d_ff_4_q);
  and and_7 (and_7_out, d_ff_3_q, Mode);
  and and_8 (and_8_out, not_1_out, Sin);
  or or_1 (or_1_out, and_1_out, and_2_out);
  or or_2 (or_2_out, and_3_out, and_4_out);
  or or_3 (or_3_out, and_5_out, and_6_out);
  or or_4 (or_4_out, and_7_out, and_8_out);
  D_Flip_Flop d_ff_1 (.D(or_1_out), .clk(Clock_out), .Q(d_ff_1_q));  // open: Qn, preset, reset
  D_Flip_Flop d_ff_2 (.D(or_2_out), .clk(Clock_out), .Q(d_ff_2_q));  // open: Qn, preset, reset
  D_Flip_Flop d_ff_3 (.D(or_3_out), .clk(Clock_out), .Q(d_ff_3_q));  // open: Qn, preset, reset
  D_Flip_Flop d_ff_4 (.D(or_4_out), .clk(Clock_out), .Q(d_ff_4_q));  // open: Qn, preset, reset
  Button Clock (.out(Clock_out));
endmodule
