// Logisim project AZ22.circ as structural Verilog: 1 circuit, main circuit main
module main (
  input  in_1,
  input  in_2,
  input  S,
  input  A,
  input  B,
  input  C,
  input  D,
  output out_8
);

  wire button_1_out, not_1_out, shift_register_1_p10, shift_register_1_p11, shift_register_1_p12,
       shift_register_1_p13, xnor_1_out, xor_1_out;

  not not_1 (not_1_out, in_2);
  Button button_1 (.out(button_1_out));
  // Shift_Register #(.length(4)) shift_register_1: pin names not known; wires that end beside it: in_1, in_2, not_1_out, button_1_out, S, A, B, C, D, shift_register_1_p10, shift_register_1_p11, shift_register_1_p12, shift_register_1_p13
  xnor xnor_1 (xnor_1_out, shift_register_1_p10, shift_register_1_p11);
  xor xor_1 (xor_1_out, shift_register_1_p12, shift_register_1_p13);
  and and_1 (out_8, xnor_1_out, xor_1_out);
endmodule
